# Fritzing sketch wsnWiring (saved by Fritzing 0.9.4)
breadboards: 1

parts:
  Mod1 = NodeMCU V1.0
  J2 = male pin header, 5 pins [form="♂ (male)"]
  J1 = male pin header, 5 pins [form="♂ (male)"]

nets:
  N1: Mod1.RX, J2.pin5
  N2: Mod1.TX, J1.pin2

custom parts:
  NodeMCU V1.0: ESP8266 based NodeMCU
